// Logisim project 555_RS_FF_to_D_FF.circ as structural Verilog
module Inv_Mux (
  input  A0,
  input  D,
  input  B0,
  input  A1,
  input  B1,
  input  A2,
  input  B2,
  output X,
  output S,
  output C,
  output X_2,
  output S_2,
  output C_2,
  output X_3,
  output S_3,
  output C_3
);

  wire and_1_out, and_2_out, and_3_out, and_4_out, and_5_out, and_6_out, and_7_out, and_8_out, and_9_out,
       and_10_out, and_11_out, and_12_out, not_1_out, not_2_out, not_3_out, not_4_out, not_5_out, not_6_out,
       xor_1_out, xor_2_out, xor_3_out;

  not not_1 (not_1_out, A0);
  not not_2 (not_2_out, D);
  not not_3 (not_3_out, A1);
  not not_4 (not_4_out, D);
  not not_5 (not_5_out, A2);
  not not_6 (not_6_out, D);
  and and_1 (and_1_out, not_1_out, D);
  and and_2 (and_2_out, A0, not_2_out);
  and and_3 (and_3_out, not_3_out, D);
  and and_4 (and_4_out, A1, not_4_out);
  and and_5 (and_5_out, not_5_out, D);
  and and_6 (and_6_out, A2, not_6_out);
  or or_1 (X, and_1_out, and_2_out);
  or or_2 (X_2, and_3_out, and_4_out);
  or or_3 (X_3, and_5_out, and_6_out);
  xor xor_1 (xor_1_out, X, B0);
  and and_7 (and_7_out, X, B0);
  xor xor_2 (xor_2_out, X_2, B1);
  and and_8 (and_8_out, X_2, B1);
  xor xor_3 (xor_3_out, X_3, B2);
  and and_9 (and_9_out, X_3, B2);
  and and_10 (and_10_out, xor_1_out, D);
  and and_11 (and_11_out, xor_2_out, C);
  and and_12 (and_12_out, xor_3_out, C_2);
  xor xor_4 (S, xor_1_out, D);
  or or_4 (C, and_10_out, and_7_out);
  xor xor_5 (S_2, xor_2_out, C);
  or or_5 (C_2, and_11_out, and_8_out);
  xor xor_6 (S_3, xor_3_out, C_2);
  or or_6 (C_3, and_12_out, and_9_out);
endmodule

module A (
  input  A,
  input  D,
  output X
);

  wire not_1_out, not_2_out, or_1_out, or_2_out;

  not not_1 (not_1_out, A);
  not not_2 (not_2_out, D);
  or or_1 (or_1_out, A, D);
  or or_2 (or_2_out, not_1_out, not_2_out);
  and and_1 (X, or_1_out, or_2_out);
endmodule

module _555_RS_To_DFF (
  input  Data,
  input  Clock_Enable,
  output TRIGbar_SETbar,
  output Q,
  output THRES_RESET
);

  wire not_1_out, not_2_out, not_3_out, not_4_out;

  not not_1 (not_1_out, Data);
  not not_2 (not_2_out, Clock_Enable);
  not not_3 (not_3_out, Data);
  or or_1 (TRIGbar_SETbar, not_1_out, not_2_out);
  and and_1 (THRES_RESET, not_3_out, Clock_Enable);
  not not_4 (not_4_out, TRIGbar_SETbar);
  S_R_Flip_Flop #(.trigger("high")) s_r_ff_1 (
    .S(not_4_out), .clk(1'b1), .R(THRES_RESET), .Q(Q));  // open: Qn, preset, reset, en
endmodule
