// Logisim project Rip_Carry_Full_Adder-Subtractor_1bit_Sim.circ as structural Verilog
module Inv_Mux (
  input  A,
  input  D,
  input  B,
  output X,
  output S,
  output C
);

  wire and_1_out, and_2_out, and_3_out, and_4_out, not_1_out, not_2_out, xor_1_out;

  not not_1 (not_1_out, A);
  not not_2 (not_2_out, D);
  and and_1 (and_1_out, not_1_out, D);
  and and_2 (and_2_out, A, not_2_out);
  or or_1 (X, and_1_out, and_2_out);
  xor xor_1 (xor_1_out, X, B);
  and and_3 (and_3_out, X, B);
  xor xor_2 (S, xor_1_out, D);
  and and_4 (and_4_out, xor_1_out, D);
  or or_2 (C, and_4_out, and_3_out);
endmodule

module A (
  input  A,
  input  D,
  output X
);

  wire not_1_out, not_2_out, or_1_out, or_2_out;

  not not_1 (not_1_out, A);
  not not_2 (not_2_out, D);
  or or_1 (or_1_out, A, D);
  or or_2 (or_2_out, not_1_out, not_2_out);
  and and_1 (X, or_1_out, or_2_out);
endmodule
