// Logisim project Rip_Carry_Full_Adder_1bit_Sim_Logisim.circ as structural Verilog: 1 circuit, main circuit main
module main (
  input  A,
  input  B,
  input  CIN
);

  wire adder_1_cout, adder_1_out, and_1_out, and_2_out, nor_1_out, not_1_out, xor_1_out, xor_2_out;

  xor xor_1 (xor_1_out, A, B);
  Adder #(.width(1)) adder_1 (.a(A), .b(B), .out(adder_1_out), .cin(CIN), .cout(adder_1_cout));
  LED S (.in(adder_1_out));
  LED Cout (.in(adder_1_cout));
  xor xor_2 (xor_2_out, xor_1_out, CIN);
  and and_1 (and_1_out, xor_1_out, CIN);
  and and_2 (and_2_out, A, B);
  nor nor_1 (nor_1_out, and_1_out, and_2_out);
  LED S_2 (.in(xor_2_out));
  LED Cout_2 (.in(not_1_out));
  not not_1 (not_1_out, nor_1_out);
endmodule
